// Logisim project 16Bit_CPU.circ as structural Verilog: 10 circuits, main circuit project_ao
module project_ao (
  input  [15:0] A,
  input  [15:0] B,
  input  [3:0] sel,
  input  [3:0] in_4,
  input  [3:0] in_5,
  input  [3:0] in_6,
  input  [3:0] in_7,
  output [15:0] Result
);

  wire [15:0] adder_1_out, and_1_out, divider_1_out, divider_2_rem, multiplier_1_out, negator_1_out,
       negator_2_out, or_1_out, shifter_1_out, shifter_2_out, shifter_3_out, shifter_4_out, subtractor_1_out,
       xor_1_out;

  Adder #(.width(16)) adder_1 (.a(A), .b(B), .out(adder_1_out));  // open: cin, cout
  assign and_1_out = A & B;  // AND_Gate and_1, 16 bits wide
  assign or_1_out = A | B;  // OR_Gate or_1, 16 bits wide
  Divider #(.width(16)) divider_1 (.a(A), .b(B), .out(divider_1_out));  // open: upper, rem
  Divider #(.width(16)) divider_2 (.a(A), .b(B), .rem(divider_2_rem));  // open: out, upper
  Multiplier #(.width(16)) multiplier_1 (.a(A), .b(B), .out(multiplier_1_out));  // open: cin, cout
  Subtractor #(.width(16)) subtractor_1 (.a(A), .b(B), .out(subtractor_1_out));  // open: bin, bout
  Shifter #(.width(16)) shifter_1 (.in(A), .\dist (in_4), .out(shifter_1_out));
  Shifter #(.width(16)) shifter_2 (.in(B), .\dist (in_5), .out(shifter_2_out));
  Shifter #(.shift("lr"), .width(16)) shifter_3 (.in(A), .\dist (in_6), .out(shifter_3_out));
  Shifter #(.shift("lr"), .width(16)) shifter_4 (.in(B), .\dist (in_7), .out(shifter_4_out));
  Negator #(.width(16)) negator_1 (.in(A), .out(negator_1_out));
  Negator #(.width(16)) negator_2 (.in(B), .out(negator_2_out));
  assign xor_1_out = A ^ B;  // XOR_Gate xor_1, 16 bits wide
  Multiplexer #(.select(4), .width(16)) multiplexer_1 (
    .in0(adder_1_out), .in1(and_1_out), .in2(or_1_out), .in3(xor_1_out), .in4(divider_1_out),
    .in5(divider_2_rem), .in6(multiplier_1_out), .in7(subtractor_1_out), .in8(shifter_1_out),
    .in9(shifter_2_out), .in10(shifter_3_out), .in11(shifter_4_out), .in12(negator_1_out),
    .in13(negator_2_out), .out(Result), .sel(sel));  // open: in14, in15
endmodule

module project_ro (
  input  [15:0] A,
  input  [15:0] B,
  input  [2:0] sel,
  output result
);

  wire comparator_1_gt, comparator_2_eq, comparator_3_gt, comparator_4_lt, comparator_5_lt, not_1_out,
       or_1_out, or_2_out;

  Comparator #(.width(16)) comparator_1 (.a(A), .b(B), .gt(comparator_1_gt));  // open: eq, lt
  Comparator #(.width(16)) comparator_2 (.a(A), .b(B), .eq(comparator_2_eq));  // open: gt, lt
  Comparator #(.width(16)) comparator_3 (.a(A), .b(B), .gt(comparator_3_gt));  // open: eq, lt
  Comparator #(.width(16)) comparator_4 (.a(A), .b(B), .lt(comparator_4_lt));  // open: gt, eq
  Comparator #(.width(16)) comparator_5 (.a(A), .b(B), .lt(comparator_5_lt));  // open: gt, eq
  or or_1 (or_1_out, comparator_3_gt, comparator_2_eq);
  or or_2 (or_2_out, comparator_5_lt, comparator_2_eq);
  not not_1 (not_1_out, comparator_2_eq);
  Multiplexer #(.select(3)) multiplexer_1 (
    .in0(comparator_1_gt), .in1(comparator_2_eq), .in2(or_1_out), .in3(comparator_4_lt), .in4(or_2_out),
    .in5(not_1_out), .out(result), .sel(sel));  // open: in6, in7

  // Notes on the sheet:
  //   A > B
  //   A == B
  //   A >= B
  //   A < B
  //   A <= B
  //   A != B
endmodule

module project_alu (
  input  [15:0] A,
  input  [15:0] B,
  input  [3:0] AUSel,
  input  OE,
  input  [2:0] RUSel,
  output [15:0] AUResult,
  output [15:0] AUDout,
  output RUResult
);

  project_ao project_ao_1 (.A(A), .B(B), .sel(AUSel), .Result(AUResult));  // open: in_4, in_5, in_6, in_7
  project_ro project_ro_1 (.A(A), .B(B), .sel(RUSel), .result(RUResult));
  assign AUDout = OE ? AUResult : 16'bz;  // Controlled_Buffer controlled_buffer_1
endmodule

module Datapath (
  input  [15:0] Test_data,
  input  oe,
  input  we,
  input  reset,
  input  oe_2,
  input  oe_3,
  input  we_2,
  input  we_3,
  input  reset_2,
  input  oe_4,
  input  reset_3,
  input  oe_5,
  input  in_13,
  input  in_14,
  input  in_15,
  input  in_16,
  input  [3:0] AUSel,
  input  in_18,
  input  oe_6,
  input  [2:0] RUSel,
  input  in_21,
  input  in_22,
  output [7:0] MARstored,
  output [15:0] IRstored,
  output [15:0] RegAdata,
  output [15:0] MBR_Data,
  output [15:0] outputregdata,
  output [15:0] AU_result,
  output RU_result,
  output [15:0] RegBstored
);

  wire clock_1_out;
  wire [7:0] bitselector_1_out, MAR_dout;
  wire [15:0] project_alu_1_audout, reg16bits_1_dout;

  Clock clock_1 (.out(clock_1_out));
  BitSelector #(.group(8), .width(16)) bitselector_1 (.in(reg16bits_1_dout), .out(bitselector_1_out), .sel(1'b0));
  reg16bits reg16bits_1 (
    .Data(project_alu_1_audout), .we(we_3), .clk(clock_1_out), .reset(reset_3), .OE(oe_5), .Result(IRstored),
    .Dout(reg16bits_1_dout));  // open: EightLSB, EightMSB
  reg16bits reg16bits_2 (
    .Data(project_alu_1_audout), .we(in_13), .clk(clock_1_out), .reset(in_14), .Result(RegAdata));  // open: OE, Dout, EightLSB, EightMSB
  project_alu project_alu_1 (
    .A(RegAdata), .B(RegBstored), .AUSel(AUSel), .OE(oe_6), .RUSel(RUSel), .AUResult(AU_result),
    .AUDout(project_alu_1_audout), .RUResult(RU_result));
  reg16bits reg16bits_3 (
    .Data(project_alu_1_audout), .we(in_21), .clk(clock_1_out), .reset(in_22), .Result(RegBstored));  // open: OE, Dout, EightLSB, EightMSB
  LED led_1 (.in(project_alu_1_audout[15]));
  LED led_2 (.in(project_alu_1_audout[14]));
  LED led_3 (.in(project_alu_1_audout[13]));
  LED led_4 (.in(project_alu_1_audout[12]));
  assign project_alu_1_audout = oe ? Test_data : 16'bz;  // Controlled_Buffer controlled_buffer_1
  LED led_5 (.in(project_alu_1_audout[9]));
  LED led_6 (.in(project_alu_1_audout[11]));
  LED led_7 (.in(project_alu_1_audout[10]));
  LED led_8 (.in(project_alu_1_audout[8]));
  LED led_9 (.in(project_alu_1_audout[7]));
  LED led_10 (.in(project_alu_1_audout[6]));
  LED led_11 (.in(project_alu_1_audout[5]));
  LED led_12 (.in(project_alu_1_audout[4]));
  LED led_13 (.in(project_alu_1_audout[3]));
  LED led_14 (.in(project_alu_1_audout[2]));
  LED led_15 (.in(project_alu_1_audout[1]));
  LED led_16 (.in(project_alu_1_audout[0]));
  reg16bits Outputreg (
    .Data(project_alu_1_audout), .we(in_15), .clk(clock_1_out), .reset(in_16), .OE(in_18),
    .Result(outputregdata), .Dout(project_alu_1_audout));  // open: EightLSB, EightMSB
  assign project_alu_1_audout = oe_3 ? MBR_Data : 16'bz;  // Controlled_Buffer controlled_buffer_2
  reg8bits MAR (
    .Data(bitselector_1_out), .we(we), .clk(clock_1_out), .Reset(reset), .oe(oe_2), .Result(MARstored),
    .Dout(MAR_dout));
  reg16bits MBR (
    .Data(project_alu_1_audout), .we(we_2), .clk(clock_1_out), .reset(reset_2), .OE(oe_4), .Result(MBR_Data),
    .Dout(project_alu_1_audout));  // open: EightLSB, EightMSB
  LED led_17 (.in(project_alu_1_audout[15]));
  LED led_18 (.in(project_alu_1_audout[14]));
  LED led_19 (.in(project_alu_1_audout[13]));
  LED led_20 (.in(project_alu_1_audout[12]));
  LED led_21 (.in(project_alu_1_audout[11]));
  LED led_22 (.in(project_alu_1_audout[8]));
  LED led_23 (.in(project_alu_1_audout[10]));
  LED led_24 (.in(project_alu_1_audout[9]));
  LED led_25 (.in(project_alu_1_audout[7]));
  LED led_26 (.in(project_alu_1_audout[6]));
  LED led_27 (.in(project_alu_1_audout[5]));
  LED led_28 (.in(project_alu_1_audout[4]));
  LED led_29 (.in(project_alu_1_audout[3]));
  LED led_30 (.in(project_alu_1_audout[2]));
  LED led_31 (.in(project_alu_1_audout[1]));
  LED led_32 (.in(project_alu_1_audout[0]));

  // Notes on the sheet:
  //   D15
  //   D14
  //   D13
  //   D12
  //   D11
  //   D9
  //   D10
  //   Internal Address Bus (8 bits)
  //   D8
  //   Internal Data Bus
  //   D7
  //   D4
  //   D6
  //   D5
  //   D2
  //   D3
  //   D1
  //   D0
  //   D15
  //   D14
  //   D13
  //   D12
  //   D11
  //   D8
  //   D9
  //   D10
  //   Internal Data Bus
  //   D7
  //   D6
  //   D5
  //   D4
  //   D3
  //   D2
  //   D1
  //   D0
endmodule

module reg16bits (
  input  [15:0] Data,
  input  we,
  input  clk,
  input  reset,
  input  OE,
  output [15:0] Result,
  output [15:0] Dout,
  output [7:0] EightLSB,
  output [7:0] EightMSB
);

  Register #(.width(16)) register_1 (.D(Data), .en(we), .clk(clk), .Q(Result), .clr(reset));
  assign Dout = OE ? Result : 16'bz;  // Controlled_Buffer controlled_buffer_1
  BitSelector #(.group(8), .width(16)) bitselector_1 (.in(Dout), .out(EightLSB), .sel(1'b0));
  BitSelector #(.group(8), .width(16)) bitselector_2 (.in(Dout), .out(EightMSB), .sel(1'b1));
endmodule

module reg8bits (
  input  [7:0] Data,
  input  we,
  input  clk,
  input  Reset,
  input  oe,
  output [7:0] Result,
  output [7:0] Dout
);

  Register register_1 (.D(Data), .en(we), .clk(clk), .Q(Result), .clr(Reset));
  assign Dout = oe ? Result : 8'bz;  // Controlled_Buffer controlled_buffer_1
endmodule

module decimal_decoder (
  input  [15:0] Din,
  output [31:0] Dout
);

  ROM #(.addrWidth(16), .dataWidth(32)) rom_1 (
    .addr(Din),
    .data({Dout[31:28], Dout[15:12], Dout[27:24], Dout[11:8], Dout[23:20], Dout[7:4], Dout[19:16], Dout[3:0]}));

  // Notes on the sheet:
  //   contents of rom_1 (hex, n*v repeats v):
  //   e7 21 cb 6b 2d 6e ee 23 ef 2f 21e7 2121 21cb 216b 212d 216e 21ee 2123 21ef 212f cbe7 cb21 cbcb cb6b
  //   cb2d cb6e cbee cb23 cbef cb2f 6be7 6b21 6bcb 6b6b 6b2d 6b6e 6bee 6b23 6bef 6b2f 2de7 2d21 2dcb 2d6b
  //   2d2d 2d6e 2dee 2d23 2def 2d2f 6ee7 6e21 6ecb 6e6b 6e2d 6e6e 6eee 6e23 6eef 6e2f eee7 ee21 eecb ee6b
  //   ee2d ee6e eeee ee23 eeef ee2f 23e7 2321 23cb 236b 232d 236e 23ee 2323 23ef 232f efe7 ef21 efcb ef6b
  //   ef2d ef6e efee ef23 efef ef2f 2fe7 2f21 2fcb 2f6b 2f2d 2f6e 2fee 2f23 2fef 2f2f 21e7e7 21e721 21e7cb
  //   21e76b 21e72d 21e76e 21e7ee 21e723 21e7ef 21e72f 2121e7 212121 2121cb 21216b 21212d 21216e 2121ee
  //   212123 2121ef 21212f 21cbe7 21cb21 21cbcb 21cb6b 21cb2d 21cb6e 21cbee 21cb23 21cbef 21cb2f 216be7
  //   216b21 216bcb 216b6b 216b2d 216b6e 216bee 216b23 216bef 216b2f 212de7 212d21 212dcb 212d6b 212d2d
  //   212d6e 212dee 212d23 212def 212d2f 216ee7 216e21 216ecb 216e6b 216e2d 216e6e 216eee 216e23 216eef
  //   216e2f 21eee7 21ee21 21eecb 21ee6b 21ee2d 21ee6e 21eeee 21ee23 21eeef 21ee2f 2123e7 212321 2123cb
  //   21236b 21232d 21236e 2123ee 212323 2123ef 21232f 21efe7 21ef21 21efcb 21ef6b 21ef2d 21ef6e 21efee
  //   21ef23 21efef 21ef2f 212fe7 212f21 212fcb 212f6b 212f2d 212f6e 212fee 212f23 212fef 212f2f cbe7e7
  //   cbe721 cbe7cb cbe76b cbe72d cbe76e cbe7ee cbe723 cbe7ef cbe72f cb21e7 cb2121 cb21cb cb216b cb212d
  //   cb216e cb21ee cb2123 cb21ef cb212f cbcbe7 cbcb21 cbcbcb cbcb6b cbcb2d cbcb6e cbcbee cbcb23 cbcbef
  //   cbcb2f cb6be7 cb6b21 cb6bcb cb6b6b cb6b2d cb6b6e cb6bee cb6b23 cb6bef cb6b2f cb2de7 cb2d21 cb2dcb
  //   cb2d6b cb2d2d cb2d6e cb2dee cb2d23 cb2def cb2d2f cb6ee7 cb6e21 cb6ecb cb6e6b cb6e2d cb6e6e
endmodule

module CU (
  input  OPC7,
  input  OPC6,
  input  OPC5,
  input  OPC4,
  input  OPC3,
  input  OPC2,
  input  OPC1,
  input  OPC0,
  input  SC2,
  input  SC1,
  input  SC0,
  output C0,
  output C1,
  output C2,
  output C3,
  output C4,
  output C5,
  output C6,
  output C7,
  output C8,
  output C9,
  output C10,
  output C11,
  output C12,
  output C13,
  output C14,
  output C15
);

  wire and_4_out, and_5_out, and_6_out, and_7_out, and_8_out, and_9_out, and_10_out, and_13_out, and_14_out,
       and_15_out, and_16_out, and_17_out, and_18_out, and_19_out, not_1_out, not_2_out, not_3_out,
       not_4_out, not_5_out, not_6_out, not_7_out, not_8_out, not_9_out, not_10_out, not_11_out;

  not not_1 (not_1_out, OPC7);
  not not_2 (not_2_out, OPC6);
  not not_3 (not_3_out, OPC5);
  not not_4 (not_4_out, OPC4);
  not not_5 (not_5_out, OPC3);
  not not_6 (not_6_out, OPC2);
  not not_7 (not_7_out, OPC1);
  not not_8 (not_8_out, OPC0);
  not not_9 (not_9_out, SC2);
  not not_10 (not_10_out, SC1);
  not not_11 (not_11_out, SC0);
  and and_1 (C0, not_9_out, not_10_out, not_11_out);
  and and_2 (C1, not_9_out, not_10_out, SC0);
  and and_3 (C2, OPC1, SC2);
  and and_4 (and_4_out, not_9_out, not_10_out, SC0);
  and and_5 (and_5_out, not_7_out, SC2, not_10_out, not_11_out);
  and and_6 (and_6_out, not_9_out, not_10_out, SC0);
  and and_7 (and_7_out, not_7_out, SC2, not_10_out, not_11_out);
  and and_8 (and_8_out, OPC1, OPC0, SC0);
  and and_9 (and_9_out, not_9_out, SC1, not_11_out);
  and and_10 (and_10_out, SC2, not_10_out, SC0);
  and and_11 (C6, OPC1, SC2);
  and and_12 (C7, not_9_out, SC1, not_11_out);
  and and_13 (and_13_out, not_7_out, not_9_out, SC1, SC0);
  and and_14 (and_14_out, OPC0, not_9_out, SC1, SC0);
  and and_15 (and_15_out, not_9_out, not_10_out, not_11_out);
  and and_16 (and_16_out, not_7_out, not_9_out, SC1, SC0);
  and and_17 (and_17_out, OPC0, not_9_out, SC1, SC0);
  and and_18 (and_18_out, not_9_out, not_10_out, SC0);
  and and_19 (and_19_out, SC2, not_10_out, not_11_out);
  and and_20 (C11, OPC1, not_8_out, SC1, SC0);
  and and_21 (C12, not_1_out, not_2_out, not_3_out, not_4_out, not_5_out, not_6_out, not_7_out, not_8_out, SC2, not_10_out, SC0);
  and and_22 (C13, OPC0, SC2, not_10_out, SC0);
  and and_23 (C14, OPC1, OPC0, SC1, SC0);
  and and_24 (C15, OPC1, not_8_out, SC1, SC0);
  or or_1 (C3, and_4_out, and_5_out);
  or or_2 (C4, and_6_out, and_7_out, and_8_out);
  or or_3 (C5, and_9_out, and_10_out);
  or or_4 (C8, and_13_out, and_14_out);
  or or_5 (C9, and_15_out, and_16_out, and_17_out);
  or or_6 (C10, and_18_out, and_19_out);
endmodule

module CPU1 (
  input  [15:0] Test_data,
  input  in_2,
  input  [7:0] in_3,
  input  oe,
  input  in_5,
  input  in_6,
  input  reset,
  input  in_8,
  input  reset_2,
  input  [3:0] AUselector,
  input  [2:0] RUselector,
  input  in_12,
  output [7:0] MAR_content,
  output [7:0] out_14,
  output [15:0] IR_content,
  output [15:0] RegAstored,
  output [15:0] MBR_content,
  output [15:0] outputregstored,
  output [15:0] AU_result,
  output RU_result,
  output [15:0] RegBstored,
  output [2:0] sc_content
);

  wire clk_out, cu_1_c0, cu_1_c1, cu_1_c2, cu_1_c3, cu_1_c4, cu_1_c5, cu_1_c6, cu_1_c7, cu_1_c8, cu_1_c9,
       cu_1_c10, cu_1_c11, cu_1_c12, cu_1_c13, cu_1_c14, cu_1_c15;
  wire [7:0] bitselector_2_out, controlled_buffer_1_out, reg8bits_1_dout;
  wire [15:0] bit_extender_1_out, bit_extender_2_out, project_alu_1_audout, ram_1_dout, reg16bits_1_dout;
  wire [31:0] decimal_decoder_1_dout, decimal_decoder_2_dout, decimal_decoder_3_dout, decimal_decoder_4_dout,
       decimal_decoder_5_dout;

  decimal_decoder decimal_decoder_1 (.Din(RegAstored), .Dout(decimal_decoder_1_dout));
  _7_Segment_Display u_7_segment_display_1 (
    .g(decimal_decoder_1_dout[15]), .f(decimal_decoder_1_dout[14]), .a(decimal_decoder_1_dout[13]),
    .b(decimal_decoder_1_dout[12]), .e(decimal_decoder_1_dout[31]), .d(decimal_decoder_1_dout[30]),
    .c(decimal_decoder_1_dout[29]), .dp(decimal_decoder_1_dout[28]));
  _7_Segment_Display u_7_segment_display_2 (
    .g(decimal_decoder_1_dout[11]), .f(decimal_decoder_1_dout[10]), .a(decimal_decoder_1_dout[9]),
    .b(decimal_decoder_1_dout[8]), .e(decimal_decoder_1_dout[27]), .d(decimal_decoder_1_dout[26]),
    .c(decimal_decoder_1_dout[25]), .dp(decimal_decoder_1_dout[24]));
  _7_Segment_Display u_7_segment_display_3 (
    .g(decimal_decoder_1_dout[7]), .f(decimal_decoder_1_dout[6]), .a(decimal_decoder_1_dout[5]),
    .b(decimal_decoder_1_dout[4]), .e(decimal_decoder_1_dout[23]), .d(decimal_decoder_1_dout[22]),
    .c(decimal_decoder_1_dout[21]), .dp(decimal_decoder_1_dout[20]));
  _7_Segment_Display u_7_segment_display_4 (
    .g(decimal_decoder_1_dout[3]), .f(decimal_decoder_1_dout[2]), .a(decimal_decoder_1_dout[1]),
    .b(decimal_decoder_1_dout[0]), .e(decimal_decoder_1_dout[19]), .d(decimal_decoder_1_dout[18]),
    .c(decimal_decoder_1_dout[17]), .dp(decimal_decoder_1_dout[16]));
  decimal_decoder decimal_decoder_2 (.Din(RegBstored), .Dout(decimal_decoder_2_dout));
  _7_Segment_Display u_7_segment_display_5 (
    .g(decimal_decoder_2_dout[15]), .f(decimal_decoder_2_dout[14]), .a(decimal_decoder_2_dout[13]),
    .b(decimal_decoder_2_dout[12]), .e(decimal_decoder_2_dout[31]), .d(decimal_decoder_2_dout[30]),
    .c(decimal_decoder_2_dout[29]), .dp(decimal_decoder_2_dout[28]));
  _7_Segment_Display u_7_segment_display_6 (
    .g(decimal_decoder_2_dout[11]), .f(decimal_decoder_2_dout[10]), .a(decimal_decoder_2_dout[9]),
    .b(decimal_decoder_2_dout[8]), .e(decimal_decoder_2_dout[27]), .d(decimal_decoder_2_dout[26]),
    .c(decimal_decoder_2_dout[25]), .dp(decimal_decoder_2_dout[24]));
  assign bit_extender_1_out = {{8{1'b0}}, out_14};  // Bit_Extender bit_extender_1
  _7_Segment_Display u_7_segment_display_7 (
    .g(decimal_decoder_2_dout[7]), .f(decimal_decoder_2_dout[6]), .a(decimal_decoder_2_dout[5]),
    .b(decimal_decoder_2_dout[4]), .e(decimal_decoder_2_dout[23]), .d(decimal_decoder_2_dout[22]),
    .c(decimal_decoder_2_dout[21]), .dp(decimal_decoder_2_dout[20]));
  _7_Segment_Display u_7_segment_display_8 (
    .g(decimal_decoder_2_dout[3]), .f(decimal_decoder_2_dout[2]), .a(decimal_decoder_2_dout[1]),
    .b(decimal_decoder_2_dout[0]), .e(decimal_decoder_2_dout[19]), .d(decimal_decoder_2_dout[18]),
    .c(decimal_decoder_2_dout[17]), .dp(decimal_decoder_2_dout[16]));
  decimal_decoder decimal_decoder_3 (.Din(bit_extender_1_out), .Dout(decimal_decoder_3_dout));
  Counter #(.max('h3)) PC (
    .count(cu_1_c1), .clk(clk_out), .D(controlled_buffer_1_out), .Q(out_14));  // open: clr, load, up, carry
  Clock clk (.out(clk_out));
  _7_Segment_Display u_7_segment_display_9 (
    .g(decimal_decoder_3_dout[3]), .f(decimal_decoder_3_dout[2]), .a(decimal_decoder_3_dout[1]),
    .b(decimal_decoder_3_dout[0]), .e(decimal_decoder_3_dout[19]), .d(decimal_decoder_3_dout[18]),
    .c(decimal_decoder_3_dout[17]), .dp(decimal_decoder_3_dout[16]));
  assign controlled_buffer_1_out = cu_1_c0 ? out_14 : 8'bz;  // Controlled_Buffer controlled_buffer_1
  BitSelector #(.group(8), .width(16)) bitselector_1 (.in(reg16bits_1_dout), .out(controlled_buffer_1_out), .sel(1'b0));
  reg16bits reg16bits_1 (
    .Data(project_alu_1_audout), .we(cu_1_c7), .clk(clk_out), .reset(reset), .OE(cu_1_c8),
    .Result(IR_content), .Dout(reg16bits_1_dout));  // open: EightLSB, EightMSB
  reg16bits reg16bits_2 (
    .Data(project_alu_1_audout), .we(cu_1_c12), .clk(clk_out), .reset(in_8), .Result(RegAstored));  // open: OE, Dout, EightLSB, EightMSB
  project_alu project_alu_1 (
    .A(RegAstored), .B(RegBstored), .AUSel(AUselector), .OE(cu_1_c11), .RUSel(RUselector),
    .AUResult(AU_result), .AUDout(project_alu_1_audout), .RUResult(RU_result));
  reg16bits reg16bits_3 (
    .Data(project_alu_1_audout), .we(cu_1_c13), .clk(clk_out), .reset(in_12), .Result(RegBstored));  // open: OE, Dout, EightLSB, EightMSB
  LED led_1 (.in(project_alu_1_audout[15]));
  LED led_2 (.in(project_alu_1_audout[14]));
  LED led_3 (.in(project_alu_1_audout[13]));
  LED led_4 (.in(project_alu_1_audout[12]));
  LED led_5 (.in(project_alu_1_audout[11]));
  LED led_6 (.in(project_alu_1_audout[10]));
  assign project_alu_1_audout = in_2 ? Test_data : 16'bz;  // Controlled_Buffer controlled_buffer_2
  LED led_7 (.in(project_alu_1_audout[9]));
  LED led_8 (.in(project_alu_1_audout[8]));
  LED led_9 (.in(project_alu_1_audout[7]));
  LED led_10 (.in(project_alu_1_audout[6]));
  LED led_11 (.in(project_alu_1_audout[5]));
  LED led_12 (.in(project_alu_1_audout[4]));
  LED led_13 (.in(project_alu_1_audout[3]));
  LED led_14 (.in(project_alu_1_audout[2]));
  LED led_15 (.in(project_alu_1_audout[1]));
  LED led_16 (.in(project_alu_1_audout[0]));
  reg16bits reg16bits_4 (
    .Data(project_alu_1_audout), .we(cu_1_c15), .clk(clk_out), .reset(reset_2), .OE(cu_1_c14),
    .Result(outputregstored), .Dout(project_alu_1_audout));  // open: EightLSB, EightMSB
  assign project_alu_1_audout = cu_1_c5 ? MBR_content : 16'bz;  // Controlled_Buffer controlled_buffer_3
  decimal_decoder decimal_decoder_4 (.Din(outputregstored), .Dout(decimal_decoder_4_dout));
  reg8bits reg8bits_1 (
    .Data(controlled_buffer_1_out), .we(cu_1_c9), .clk(clk_out), .Reset(in_5), .oe(cu_1_c10),
    .Result(MAR_content), .Dout(reg8bits_1_dout));
  reg16bits reg16bits_5 (
    .Data(project_alu_1_audout), .we(cu_1_c4), .clk(clk_out), .reset(in_6), .OE(cu_1_c6),
    .Result(MBR_content), .Dout(project_alu_1_audout));  // open: EightLSB, EightMSB
  _7_Segment_Display u_7_segment_display_10 (
    .g(decimal_decoder_4_dout[15]), .f(decimal_decoder_4_dout[14]), .a(decimal_decoder_4_dout[13]),
    .b(decimal_decoder_4_dout[12]), .e(decimal_decoder_4_dout[31]), .d(decimal_decoder_4_dout[30]),
    .c(decimal_decoder_4_dout[29]), .dp(decimal_decoder_4_dout[28]));
  _7_Segment_Display u_7_segment_display_11 (
    .g(decimal_decoder_4_dout[11]), .f(decimal_decoder_4_dout[10]), .a(decimal_decoder_4_dout[9]),
    .b(decimal_decoder_4_dout[8]), .e(decimal_decoder_4_dout[27]), .d(decimal_decoder_4_dout[26]),
    .c(decimal_decoder_4_dout[25]), .dp(decimal_decoder_4_dout[24]));
  _7_Segment_Display u_7_segment_display_12 (
    .g(decimal_decoder_4_dout[7]), .f(decimal_decoder_4_dout[6]), .a(decimal_decoder_4_dout[5]),
    .b(decimal_decoder_4_dout[4]), .e(decimal_decoder_4_dout[23]), .d(decimal_decoder_4_dout[22]),
    .c(decimal_decoder_4_dout[21]), .dp(decimal_decoder_4_dout[20]));
  assign reg8bits_1_dout = oe ? in_3 : 8'bz;  // Controlled_Buffer controlled_buffer_4
  LED led_17 (.in(project_alu_1_audout[15]));
  _7_Segment_Display u_7_segment_display_13 (
    .g(decimal_decoder_4_dout[3]), .f(decimal_decoder_4_dout[2]), .a(decimal_decoder_4_dout[1]),
    .b(decimal_decoder_4_dout[0]), .e(decimal_decoder_4_dout[19]), .d(decimal_decoder_4_dout[18]),
    .c(decimal_decoder_4_dout[17]), .dp(decimal_decoder_4_dout[16]));
  LED led_18 (.in(project_alu_1_audout[14]));
  LED led_19 (.in(project_alu_1_audout[13]));
  LED led_20 (.in(project_alu_1_audout[12]));
  LED led_21 (.in(project_alu_1_audout[11]));
  LED led_22 (.in(project_alu_1_audout[10]));
  LED led_23 (.in(project_alu_1_audout[9]));
  LED led_24 (.in(project_alu_1_audout[8]));
  LED led_25 (.in(project_alu_1_audout[7]));
  LED led_26 (.in(project_alu_1_audout[6]));
  LED led_27 (.in(project_alu_1_audout[5]));
  LED led_28 (.in(project_alu_1_audout[4]));
  LED led_29 (.in(project_alu_1_audout[3]));
  LED led_30 (.in(project_alu_1_audout[2]));
  LED led_31 (.in(project_alu_1_audout[1]));
  LED led_32 (.in(project_alu_1_audout[0]));
  assign project_alu_1_audout = cu_1_c3 ? ram_1_dout : 16'bz;  // Controlled_Buffer controlled_buffer_5
  BitSelector #(.group(8), .width(16)) bitselector_2 (.in(IR_content), .out(bitselector_2_out), .sel(1'b1));
  Counter #(.max('h5), .width(3)) counter_1 (.clk(clk_out), .Q(sc_content));  // open: clr, load, up, count, D, carry
  assign bit_extender_2_out = {{13{1'b0}}, sc_content};  // Bit_Extender bit_extender_2
  CU cu_1 (
    .OPC7(bitselector_2_out[7]), .OPC6(bitselector_2_out[6]), .OPC5(bitselector_2_out[5]),
    .OPC4(bitselector_2_out[4]), .OPC3(bitselector_2_out[3]), .OPC2(bitselector_2_out[2]),
    .OPC1(bitselector_2_out[1]), .OPC0(bitselector_2_out[0]), .SC2(sc_content[2]), .SC1(sc_content[1]),
    .SC0(sc_content[0]), .C0(cu_1_c0), .C1(cu_1_c1), .C2(cu_1_c2), .C3(cu_1_c3), .C4(cu_1_c4), .C5(cu_1_c5),
    .C6(cu_1_c6), .C7(cu_1_c7), .C8(cu_1_c8), .C9(cu_1_c9), .C10(cu_1_c10), .C11(cu_1_c11), .C12(cu_1_c12),
    .C13(cu_1_c13), .C14(cu_1_c14), .C15(cu_1_c15));
  decimal_decoder decimal_decoder_5 (.Din(bit_extender_2_out), .Dout(decimal_decoder_5_dout));
  _7_Segment_Display u_7_segment_display_14 (
    .g(decimal_decoder_5_dout[3]), .f(decimal_decoder_5_dout[2]), .a(decimal_decoder_5_dout[1]),
    .b(decimal_decoder_5_dout[0]), .e(decimal_decoder_5_dout[19]), .d(decimal_decoder_5_dout[18]),
    .c(decimal_decoder_5_dout[17]), .dp(decimal_decoder_5_dout[16]));
  RAM #(.dataWidth(16), .enables("line")) ram_1 (
    .addr(reg8bits_1_dout), .we(cu_1_c2), .clk(clk_out), .din(project_alu_1_audout), .dout(ram_1_dout));

  // Notes on the sheet:
  //   Instruction Register(IR)
  //   Register A
  //   ALU
  //   Register B
  //   D15
  //   D14
  //   D13
  //   D12
  //   D10
  //   D11
  //   D9
  //   D8
  //   Internal Address Bus 
  //   Internal Data Bus
  //   D7
  //   D6
  //   D5
  //   D4
  //   D3
  //   D2
  //   D1
  //   D0
  //   we
  //   oe
  //   Output Register
  //   MAR
  //   MBR
  //   External Address Bus
  //   D15
  //   D14
  //   D13
  //   D12
  //   D10
  //   D11
  //   D9
  //   D8
  //   Internal Data Bus
  //   D7
  //   we
  //   D4
  //   D6
  //   D5
  //   D2
  //   D3
  //   D1
  //   oe
  //   D0
endmodule

module CPU (
  input  [15:0] Test_data,
  input  in_2,
  input  [7:0] in_3,
  input  oe,
  input  in_5,
  input  in_6,
  input  reset,
  input  in_8,
  input  reset_2,
  input  [3:0] AUselector,
  input  [2:0] RUselector,
  input  in_12,
  output [7:0] MAR_content,
  output [7:0] out_14,
  output [15:0] IR_content,
  output [15:0] RegAstored,
  output [15:0] MBR_content,
  output [15:0] outputregstored,
  output [15:0] AU_result,
  output RU_result,
  output [15:0] RegBstored,
  output [2:0] sc_content
);

  wire clk_out, cu_1_c0, cu_1_c1, cu_1_c2, cu_1_c3, cu_1_c4, cu_1_c5, cu_1_c6, cu_1_c7, cu_1_c8, cu_1_c9,
       cu_1_c10, cu_1_c11, cu_1_c12, cu_1_c13, cu_1_c14, cu_1_c15;
  wire [7:0] bitselector_2_out, controlled_buffer_1_out, reg8bits_1_dout;
  wire [15:0] bit_extender_1_out, bit_extender_2_out, project_alu_1_audout, ram_1_dout, reg16bits_1_dout;
  wire [31:0] decimal_decoder_1_dout, decimal_decoder_2_dout, decimal_decoder_3_dout, decimal_decoder_4_dout,
       decimal_decoder_5_dout;

  decimal_decoder decimal_decoder_1 (.Din(RegAstored), .Dout(decimal_decoder_1_dout));
  _7_Segment_Display u_7_segment_display_1 (
    .g(decimal_decoder_1_dout[15]), .f(decimal_decoder_1_dout[14]), .a(decimal_decoder_1_dout[13]),
    .b(decimal_decoder_1_dout[12]), .e(decimal_decoder_1_dout[31]), .d(decimal_decoder_1_dout[30]),
    .c(decimal_decoder_1_dout[29]), .dp(decimal_decoder_1_dout[28]));
  _7_Segment_Display u_7_segment_display_2 (
    .g(decimal_decoder_1_dout[11]), .f(decimal_decoder_1_dout[10]), .a(decimal_decoder_1_dout[9]),
    .b(decimal_decoder_1_dout[8]), .e(decimal_decoder_1_dout[27]), .d(decimal_decoder_1_dout[26]),
    .c(decimal_decoder_1_dout[25]), .dp(decimal_decoder_1_dout[24]));
  _7_Segment_Display u_7_segment_display_3 (
    .g(decimal_decoder_1_dout[7]), .f(decimal_decoder_1_dout[6]), .a(decimal_decoder_1_dout[5]),
    .b(decimal_decoder_1_dout[4]), .e(decimal_decoder_1_dout[23]), .d(decimal_decoder_1_dout[22]),
    .c(decimal_decoder_1_dout[21]), .dp(decimal_decoder_1_dout[20]));
  _7_Segment_Display u_7_segment_display_4 (
    .g(decimal_decoder_1_dout[3]), .f(decimal_decoder_1_dout[2]), .a(decimal_decoder_1_dout[1]),
    .b(decimal_decoder_1_dout[0]), .e(decimal_decoder_1_dout[19]), .d(decimal_decoder_1_dout[18]),
    .c(decimal_decoder_1_dout[17]), .dp(decimal_decoder_1_dout[16]));
  decimal_decoder decimal_decoder_2 (.Din(RegBstored), .Dout(decimal_decoder_2_dout));
  _7_Segment_Display u_7_segment_display_5 (
    .g(decimal_decoder_2_dout[15]), .f(decimal_decoder_2_dout[14]), .a(decimal_decoder_2_dout[13]),
    .b(decimal_decoder_2_dout[12]), .e(decimal_decoder_2_dout[31]), .d(decimal_decoder_2_dout[30]),
    .c(decimal_decoder_2_dout[29]), .dp(decimal_decoder_2_dout[28]));
  _7_Segment_Display u_7_segment_display_6 (
    .g(decimal_decoder_2_dout[11]), .f(decimal_decoder_2_dout[10]), .a(decimal_decoder_2_dout[9]),
    .b(decimal_decoder_2_dout[8]), .e(decimal_decoder_2_dout[27]), .d(decimal_decoder_2_dout[26]),
    .c(decimal_decoder_2_dout[25]), .dp(decimal_decoder_2_dout[24]));
  assign bit_extender_1_out = {{8{1'b0}}, out_14};  // Bit_Extender bit_extender_1
  _7_Segment_Display u_7_segment_display_7 (
    .g(decimal_decoder_2_dout[7]), .f(decimal_decoder_2_dout[6]), .a(decimal_decoder_2_dout[5]),
    .b(decimal_decoder_2_dout[4]), .e(decimal_decoder_2_dout[23]), .d(decimal_decoder_2_dout[22]),
    .c(decimal_decoder_2_dout[21]), .dp(decimal_decoder_2_dout[20]));
  _7_Segment_Display u_7_segment_display_8 (
    .g(decimal_decoder_2_dout[3]), .f(decimal_decoder_2_dout[2]), .a(decimal_decoder_2_dout[1]),
    .b(decimal_decoder_2_dout[0]), .e(decimal_decoder_2_dout[19]), .d(decimal_decoder_2_dout[18]),
    .c(decimal_decoder_2_dout[17]), .dp(decimal_decoder_2_dout[16]));
  decimal_decoder decimal_decoder_3 (.Din(bit_extender_1_out), .Dout(decimal_decoder_3_dout));
  Counter #(.max('h3)) PC (
    .count(cu_1_c1), .clk(clk_out), .D(controlled_buffer_1_out), .Q(out_14));  // open: clr, load, up, carry
  Clock clk (.out(clk_out));
  _7_Segment_Display u_7_segment_display_9 (
    .g(decimal_decoder_3_dout[3]), .f(decimal_decoder_3_dout[2]), .a(decimal_decoder_3_dout[1]),
    .b(decimal_decoder_3_dout[0]), .e(decimal_decoder_3_dout[19]), .d(decimal_decoder_3_dout[18]),
    .c(decimal_decoder_3_dout[17]), .dp(decimal_decoder_3_dout[16]));
  assign controlled_buffer_1_out = cu_1_c0 ? out_14 : 8'bz;  // Controlled_Buffer controlled_buffer_1
  BitSelector #(.group(8), .width(16)) bitselector_1 (.in(reg16bits_1_dout), .out(controlled_buffer_1_out), .sel(1'b0));
  reg16bits reg16bits_1 (
    .Data(project_alu_1_audout), .we(cu_1_c7), .clk(clk_out), .reset(reset), .OE(cu_1_c8),
    .Result(IR_content), .Dout(reg16bits_1_dout));  // open: EightLSB, EightMSB
  reg16bits reg16bits_2 (
    .Data(project_alu_1_audout), .we(cu_1_c12), .clk(clk_out), .reset(in_8), .Result(RegAstored));  // open: OE, Dout, EightLSB, EightMSB
  project_alu project_alu_1 (
    .A(RegAstored), .B(RegBstored), .AUSel(AUselector), .OE(cu_1_c11), .RUSel(RUselector),
    .AUResult(AU_result), .AUDout(project_alu_1_audout), .RUResult(RU_result));
  reg16bits reg16bits_3 (
    .Data(project_alu_1_audout), .we(cu_1_c13), .clk(clk_out), .reset(in_12), .Result(RegBstored));  // open: OE, Dout, EightLSB, EightMSB
  LED led_1 (.in(project_alu_1_audout[15]));
  LED led_2 (.in(project_alu_1_audout[14]));
  LED led_3 (.in(project_alu_1_audout[13]));
  LED led_4 (.in(project_alu_1_audout[12]));
  LED led_5 (.in(project_alu_1_audout[11]));
  LED led_6 (.in(project_alu_1_audout[10]));
  assign project_alu_1_audout = in_2 ? Test_data : 16'bz;  // Controlled_Buffer controlled_buffer_2
  LED led_7 (.in(project_alu_1_audout[9]));
  LED led_8 (.in(project_alu_1_audout[8]));
  LED led_9 (.in(project_alu_1_audout[7]));
  LED led_10 (.in(project_alu_1_audout[6]));
  LED led_11 (.in(project_alu_1_audout[5]));
  LED led_12 (.in(project_alu_1_audout[4]));
  LED led_13 (.in(project_alu_1_audout[3]));
  LED led_14 (.in(project_alu_1_audout[2]));
  LED led_15 (.in(project_alu_1_audout[1]));
  LED led_16 (.in(project_alu_1_audout[0]));
  reg16bits reg16bits_4 (
    .Data(project_alu_1_audout), .we(cu_1_c15), .clk(clk_out), .reset(reset_2), .OE(cu_1_c14),
    .Result(outputregstored), .Dout(project_alu_1_audout));  // open: EightLSB, EightMSB
  assign project_alu_1_audout = cu_1_c5 ? MBR_content : 16'bz;  // Controlled_Buffer controlled_buffer_3
  decimal_decoder decimal_decoder_4 (.Din(outputregstored), .Dout(decimal_decoder_4_dout));
  reg8bits reg8bits_1 (
    .Data(controlled_buffer_1_out), .we(cu_1_c9), .clk(clk_out), .Reset(in_5), .oe(cu_1_c10),
    .Result(MAR_content), .Dout(reg8bits_1_dout));
  reg16bits reg16bits_5 (
    .Data(project_alu_1_audout), .we(cu_1_c4), .clk(clk_out), .reset(in_6), .OE(cu_1_c6),
    .Result(MBR_content), .Dout(project_alu_1_audout));  // open: EightLSB, EightMSB
  _7_Segment_Display u_7_segment_display_10 (
    .g(decimal_decoder_4_dout[15]), .f(decimal_decoder_4_dout[14]), .a(decimal_decoder_4_dout[13]),
    .b(decimal_decoder_4_dout[12]), .e(decimal_decoder_4_dout[31]), .d(decimal_decoder_4_dout[30]),
    .c(decimal_decoder_4_dout[29]), .dp(decimal_decoder_4_dout[28]));
  _7_Segment_Display u_7_segment_display_11 (
    .g(decimal_decoder_4_dout[11]), .f(decimal_decoder_4_dout[10]), .a(decimal_decoder_4_dout[9]),
    .b(decimal_decoder_4_dout[8]), .e(decimal_decoder_4_dout[27]), .d(decimal_decoder_4_dout[26]),
    .c(decimal_decoder_4_dout[25]), .dp(decimal_decoder_4_dout[24]));
  _7_Segment_Display u_7_segment_display_12 (
    .g(decimal_decoder_4_dout[7]), .f(decimal_decoder_4_dout[6]), .a(decimal_decoder_4_dout[5]),
    .b(decimal_decoder_4_dout[4]), .e(decimal_decoder_4_dout[23]), .d(decimal_decoder_4_dout[22]),
    .c(decimal_decoder_4_dout[21]), .dp(decimal_decoder_4_dout[20]));
  assign reg8bits_1_dout = oe ? in_3 : 8'bz;  // Controlled_Buffer controlled_buffer_4
  LED led_17 (.in(project_alu_1_audout[15]));
  _7_Segment_Display u_7_segment_display_13 (
    .g(decimal_decoder_4_dout[3]), .f(decimal_decoder_4_dout[2]), .a(decimal_decoder_4_dout[1]),
    .b(decimal_decoder_4_dout[0]), .e(decimal_decoder_4_dout[19]), .d(decimal_decoder_4_dout[18]),
    .c(decimal_decoder_4_dout[17]), .dp(decimal_decoder_4_dout[16]));
  LED led_18 (.in(project_alu_1_audout[14]));
  LED led_19 (.in(project_alu_1_audout[13]));
  LED led_20 (.in(project_alu_1_audout[12]));
  LED led_21 (.in(project_alu_1_audout[11]));
  LED led_22 (.in(project_alu_1_audout[10]));
  LED led_23 (.in(project_alu_1_audout[9]));
  LED led_24 (.in(project_alu_1_audout[8]));
  LED led_25 (.in(project_alu_1_audout[7]));
  LED led_26 (.in(project_alu_1_audout[6]));
  LED led_27 (.in(project_alu_1_audout[5]));
  LED led_28 (.in(project_alu_1_audout[4]));
  LED led_29 (.in(project_alu_1_audout[3]));
  LED led_30 (.in(project_alu_1_audout[2]));
  LED led_31 (.in(project_alu_1_audout[1]));
  LED led_32 (.in(project_alu_1_audout[0]));
  assign project_alu_1_audout = cu_1_c3 ? ram_1_dout : 16'bz;  // Controlled_Buffer controlled_buffer_5
  BitSelector #(.group(8), .width(16)) bitselector_2 (.in(IR_content), .out(bitselector_2_out), .sel(1'b1));
  Counter #(.max('h5), .width(3)) counter_1 (.clk(clk_out), .Q(sc_content));  // open: clr, load, up, count, D, carry
  assign bit_extender_2_out = {{13{1'b0}}, sc_content};  // Bit_Extender bit_extender_2
  CU cu_1 (
    .OPC7(bitselector_2_out[7]), .OPC6(bitselector_2_out[6]), .OPC5(bitselector_2_out[5]),
    .OPC4(bitselector_2_out[4]), .OPC3(bitselector_2_out[3]), .OPC2(bitselector_2_out[2]),
    .OPC1(bitselector_2_out[1]), .OPC0(bitselector_2_out[0]), .SC2(sc_content[2]), .SC1(sc_content[1]),
    .SC0(sc_content[0]), .C0(cu_1_c0), .C1(cu_1_c1), .C2(cu_1_c2), .C3(cu_1_c3), .C4(cu_1_c4), .C5(cu_1_c5),
    .C6(cu_1_c6), .C7(cu_1_c7), .C8(cu_1_c8), .C9(cu_1_c9), .C10(cu_1_c10), .C11(cu_1_c11), .C12(cu_1_c12),
    .C13(cu_1_c13), .C14(cu_1_c14), .C15(cu_1_c15));
  decimal_decoder decimal_decoder_5 (.Din(bit_extender_2_out), .Dout(decimal_decoder_5_dout));
  _7_Segment_Display u_7_segment_display_14 (
    .g(decimal_decoder_5_dout[3]), .f(decimal_decoder_5_dout[2]), .a(decimal_decoder_5_dout[1]),
    .b(decimal_decoder_5_dout[0]), .e(decimal_decoder_5_dout[19]), .d(decimal_decoder_5_dout[18]),
    .c(decimal_decoder_5_dout[17]), .dp(decimal_decoder_5_dout[16]));
  RAM #(.dataWidth(16), .enables("line")) ram_1 (
    .addr(reg8bits_1_dout), .we(cu_1_c2), .clk(clk_out), .din(project_alu_1_audout), .dout(ram_1_dout));

  // Notes on the sheet:
  //   Instruction Register(IR)
  //   Register A
  //   ALU
  //   Register B
  //   D15
  //   D14
  //   D13
  //   D12
  //   D10
  //   D11
  //   D9
  //   D8
  //   Internal Address Bus 
  //   Internal Data Bus
  //   D7
  //   D6
  //   D5
  //   D4
  //   D3
  //   D2
  //   D1
  //   D0
  //   we
  //   oe
  //   Output Register
  //   MAR
  //   MBR
  //   External Address Bus
  //   D15
  //   D14
  //   D13
  //   D12
  //   D10
  //   D11
  //   D9
  //   D8
  //   Internal Data Bus
  //   D7
  //   we
  //   D4
  //   D6
  //   D5
  //   D2
  //   D3
  //   D1
  //   oe
  //   D0
endmodule
